// Logisim project ex5.circ as structural Verilog: 1 circuit, main circuit num_checker
module num_checker (
  input  [31:0] num,
  input  clk,
  output is_odd,
  output is_even,
  output is_zero,
  output greater_than_fifteen,
  output five_or_ten
);

  wire and_1_out, and_2_out, comparator_2_eq, comparator_3_eq, comparator_4_eq, comparator_5_eq,
       comparator_6_eq;
  wire [7:0] adder_1_out, num_cycles_q;

  Adder adder_1 (.a(num_cycles_q), .b(8'h1), .out(adder_1_out));  // open: cin, cout
  Register num_cycles (.D(adder_1_out), .clk(clk), .Q(num_cycles_q));  // open: en, clr
  not not_1 (is_even, num[0]);
  Comparator #(.width(32)) comparator_1 (.a(num), .b({32{1'b0}}), .eq(is_zero));  // open: gt, lt
  Comparator #(.width(28)) comparator_2 (.a(num[31:4]), .b({28{1'b0}}), .eq(comparator_2_eq));  // open: gt, lt
  Comparator #(.width(3)) comparator_3 (.a(num[2:0]), .b(3'b101), .eq(comparator_3_eq));  // open: gt, lt
  Comparator #(.width(29)) comparator_4 (.a(num[31:3]), .b({29{1'b0}}), .eq(comparator_4_eq));  // open: gt, lt
  Comparator #(.width(4)) comparator_5 (.a(num[3:0]), .b(4'b1010), .eq(comparator_5_eq));  // open: gt, lt
  Comparator #(.width(28)) comparator_6 (.a(num[31:4]), .b({28{1'b0}}), .eq(comparator_6_eq));  // open: gt, lt
  not not_2 (greater_than_fifteen, comparator_2_eq);
  and and_1 (and_1_out, comparator_3_eq, comparator_4_eq);
  and and_2 (and_2_out, comparator_5_eq, comparator_6_eq);
  or or_1 (five_or_ten, and_1_out, and_2_out);

  assign is_odd = num[0];

  // Other names for the same wires on the sheet: bit_zero = num[0]; bits_five[2:0] = num[2:0];
  //   bits_ten[3:0] = num[3:0]; five_rest_zero[28:0] = num[31:3]; bits_15[27:0] = num[31:4];
  //   ten_rest_zero[27:0] = num[31:4]
endmodule
