// Logisim project branch-comp.circ as structural Verilog: 1 circuit, main circuit branch_comp
module branch_comp (
  input  [31:0] BrData1,
  input  [31:0] BrData2,
  input  BrUn,
  output BrEq,
  output BrLt
);

  wire comparator_1_eq, comparator_1_lt, comparator_2_eq, comparator_2_lt, not_1_out;

  Comparator #(.width(32)) comparator_1 (
    .a(BrData1), .b(BrData2), .eq(comparator_1_eq), .lt(comparator_1_lt));  // open: gt
  not not_1 (not_1_out, BrUn);
  Comparator #(.mode("unsigned"), .width(32)) comparator_2 (
    .a(BrData1), .b(BrData2), .eq(comparator_2_eq), .lt(comparator_2_lt));  // open: gt
  assign BrEq = not_1_out ? comparator_1_eq : 1'bz;  // Controlled_Buffer controlled_buffer_1
  assign BrLt = not_1_out ? comparator_1_lt : 1'bz;  // Controlled_Buffer controlled_buffer_2
  assign BrEq = BrUn ? comparator_2_eq : 1'bz;  // Controlled_Buffer controlled_buffer_3
  assign BrLt = BrUn ? comparator_2_lt : 1'bz;  // Controlled_Buffer controlled_buffer_4

  // Notes on the sheet:
  //   INPUTS to your circuit
  //   DON'T CHANGE THE LOCATIONS OF THE INPUTS AND OUTPUTS!
  //   OUTPUT from your circuit
endmodule
