// Logisim project control-logic.circ as structural Verilog: 1 circuit, main circuit control_logic
module control_logic (
  input  [31:0] Instruction,
  input  BrEq,
  input  BrLt,
  output PCSel,
  output RegWEn,
  output [2:0] ImmSel,
  output BrUn,
  output ASel,
  output BSel,
  output [3:0] ALUSel,
  output MemRW,
  output [1:0] WBSel
);

  wire and_1_out, and_2_out, and_3_out, and_4_out, and_5_out, and_6_out, and_7_out, is_add, is_addi, is_and,
       is_andi, is_auipc, is_B, is_beq, is_bge, is_bgeu, is_blt, is_bltu, is_bne, is_I, is_jal, is_jalr,
       is_L, is_lb, is_lh, is_lui, is_lw, is_mul, is_mulh, is_mulhu, is_or, is_ori, is_R, is_S, is_sb, is_sh,
       is_sll, is_slli, is_slt, is_slti, is_sra, is_srai, is_srl, is_srli, is_sub, is_sw, is_xor, is_xori,
       not_1_out, not_2_out, not_3_out, not_4_out, not_5_out, not_6_out, sel1, sel2, sel3, sel4;
  wire [2:0] controlled_buffer_5_out, controlled_buffer_10_out, controlled_buffer_11_out;
  wire [5:0] ROMSel;
  wire [6:0] controlled_buffer_1_out, controlled_buffer_2_out, controlled_buffer_3_out,
       controlled_buffer_4_out;
  wire [15:14] rom_1_data;

  Demultiplexer #(.enable("true"), .select(3)) demultiplexer_1 (
    .out0(sel1), .out1(sel2), .out2(is_slt), .out3(is_mulhu), .out4(is_xor), .out5(sel3), .out6(is_or),
    .out7(is_and), .in(1'b1), .sel(Instruction[14:12]), .en(is_R));
  assign controlled_buffer_1_out = sel1 ? Instruction[31:25] : 7'bz;  // Controlled_Buffer controlled_buffer_1
  assign controlled_buffer_2_out = sel2 ? Instruction[31:25] : 7'bz;  // Controlled_Buffer controlled_buffer_2
  assign controlled_buffer_3_out = sel3 ? Instruction[31:25] : 7'bz;  // Controlled_Buffer controlled_buffer_3
  assign controlled_buffer_4_out = sel4 ? Instruction[31:25] : 7'bz;  // Controlled_Buffer controlled_buffer_4
  Comparator #(.width(7)) comparator_1 (.a(7'b0000001), .b(controlled_buffer_1_out), .eq(is_mul));  // open: gt, lt
  Comparator #(.width(7)) comparator_2 (.a(7'b0100000), .b(controlled_buffer_1_out), .eq(is_sub));  // open: gt, lt
  Comparator #(.width(7)) comparator_3 (.a(controlled_buffer_1_out), .b({7{1'b0}}), .eq(is_add));  // open: gt, lt
  Comparator #(.width(7)) comparator_4 (.a(7'b0000001), .b(controlled_buffer_2_out), .eq(is_mulh));  // open: gt, lt
  Comparator #(.width(7)) comparator_5 (.a(controlled_buffer_2_out), .b({7{1'b0}}), .eq(is_sll));  // open: gt, lt
  Comparator #(.width(7)) comparator_6 (.a(7'b0000001), .b(controlled_buffer_3_out), .eq(is_srl));  // open: gt, lt
  Comparator #(.width(7)) comparator_7 (.a(controlled_buffer_3_out), .b(7'b0100000), .eq(is_sra));  // open: gt, lt
  Comparator #(.width(7)) comparator_8 (.a({7{1'b0}}), .b(controlled_buffer_4_out), .eq(is_srli));  // open: gt, lt
  Comparator #(.width(7)) comparator_9 (.a(controlled_buffer_4_out), .b(7'b0100000), .eq(is_srai));  // open: gt, lt
  ROM #(.addrWidth(6), .dataWidth(16)) rom_1 (
    .addr(ROMSel), .data({rom_1_data, WBSel, MemRW, ALUSel, BSel, ASel, BrUn, ImmSel, RegWEn}));
  Comparator #(.width(7)) comparator_10 (.a(7'b0110011), .b(Instruction[6:0]), .eq(is_R));  // open: gt, lt
  Comparator #(.width(7)) comparator_11 (.a(Instruction[6:0]), .b(7'b0000011), .eq(is_L));  // open: gt, lt
  Comparator #(.width(7)) comparator_12 (.a(Instruction[6:0]), .b(7'b0010011), .eq(is_I));  // open: gt, lt
  Comparator #(.width(7)) comparator_13 (.a(Instruction[6:0]), .b(7'b0100011), .eq(is_S));  // open: gt, lt
  Comparator #(.width(7)) comparator_14 (.a(Instruction[6:0]), .b(7'b1100011), .eq(is_B));  // open: gt, lt
  Comparator #(.width(7)) comparator_15 (.a(Instruction[6:0]), .b(7'b0010111), .eq(is_auipc));  // open: gt, lt
  Comparator #(.width(7)) comparator_16 (.a(Instruction[6:0]), .b(7'b0110111), .eq(is_lui));  // open: gt, lt
  Comparator #(.width(7)) comparator_17 (.a(Instruction[6:0]), .b(7'b1101111), .eq(is_jal));  // open: gt, lt
  Comparator #(.width(7)) comparator_18 (.a(Instruction[6:0]), .b(7'b1100111), .eq(is_jalr));  // open: gt, lt
  assign controlled_buffer_5_out = is_B ? Instruction[14:12] : 3'bz;  // Controlled_Buffer controlled_buffer_5
  Demultiplexer #(.enable("true"), .select(3)) demultiplexer_2 (
    .out0(is_addi), .out1(is_slli), .out2(is_slti), .out4(is_xori), .out5(sel4), .out6(is_ori),
    .out7(is_andi), .in(1'b1), .sel(Instruction[14:12]), .en(is_I));  // open: out3
  Comparator #(.width(3)) comparator_19 (.a(3'b000), .b(controlled_buffer_5_out), .eq(is_beq));  // open: gt, lt
  Comparator #(.width(3)) comparator_20 (.a(3'b001), .b(controlled_buffer_5_out), .eq(is_bne));  // open: gt, lt
  Comparator #(.width(3)) comparator_21 (.a(3'b100), .b(controlled_buffer_5_out), .eq(is_blt));  // open: gt, lt
  Comparator #(.width(3)) comparator_22 (.a(3'b101), .b(controlled_buffer_5_out), .eq(is_bge));  // open: gt, lt
  Comparator #(.width(3)) comparator_23 (.a(3'b110), .b(controlled_buffer_5_out), .eq(is_bltu));  // open: gt, lt
  Comparator #(.width(3)) comparator_24 (.a(3'b111), .b(controlled_buffer_5_out), .eq(is_bgeu));  // open: gt, lt
  Priority_Encoder #(.select_enc(6)) priority_encoder_1 (
    .in0(is_add), .in1(is_mul), .in2(is_sub), .in3(is_sll), .in4(is_mulh), .in5(is_mulhu), .in6(is_slt),
    .in7(is_xor), .in8(is_srl), .in9(is_sra), .in10(is_or), .in11(is_and), .in12(is_lb), .in13(is_lh),
    .in14(is_lw), .in15(is_addi), .in16(is_slli), .in17(is_slti), .in18(is_xori), .in19(is_srli),
    .in20(is_srai), .in21(is_ori), .in22(is_andi), .in23(is_sb), .in24(is_sh), .in25(is_sw), .in26(is_beq),
    .in27(is_bne), .in28(is_blt), .in29(is_bge), .in30(is_bltu), .in31(is_bgeu), .in32(is_auipc),
    .in33(is_lui), .in34(is_jal), .in35(is_jalr), .out(ROMSel));  // open: in36, in37, in38, in39, in40, in41, in42, in43, in44, in45, in46, in47, in48, in49, in50, in51, in52, in53, in54, in55, in56, in57, in58, in59, in60, in61, in62, in63, gs, en_out, en_in
  assign PCSel = and_1_out ? BrEq : 1'bz;  // Controlled_Buffer controlled_buffer_6
  and and_1 (and_1_out, is_beq, is_B);
  not not_1 (not_1_out, BrEq);
  assign PCSel = and_2_out ? not_1_out : 1'bz;  // Controlled_Buffer controlled_buffer_7
  and and_2 (and_2_out, is_bne, is_B);
  assign PCSel = and_3_out ? BrLt : 1'bz;  // Controlled_Buffer controlled_buffer_8
  and and_3 (and_3_out, is_blt, is_B);
  assign PCSel = is_jal ? 1'b1 : 1'bz;  // Controlled_Buffer controlled_buffer_9
  assign controlled_buffer_10_out = is_L ? Instruction[14:12] : 3'bz;  // Controlled_Buffer controlled_buffer_10
  assign controlled_buffer_11_out = is_S ? Instruction[14:12] : 3'bz;  // Controlled_Buffer controlled_buffer_11
  Comparator #(.width(3)) comparator_25 (.a(3'b000), .b(controlled_buffer_10_out), .eq(is_lb));  // open: gt, lt
  Comparator #(.width(3)) comparator_26 (.a(3'b001), .b(controlled_buffer_10_out), .eq(is_lh));  // open: gt, lt
  Comparator #(.width(3)) comparator_27 (.a(3'b010), .b(controlled_buffer_10_out), .eq(is_lw));  // open: gt, lt
  Comparator #(.width(3)) comparator_28 (.a(3'b000), .b(controlled_buffer_11_out), .eq(is_sb));  // open: gt, lt
  Comparator #(.width(3)) comparator_29 (.a(3'b001), .b(controlled_buffer_11_out), .eq(is_sh));  // open: gt, lt
  Comparator #(.width(3)) comparator_30 (.a(3'b010), .b(controlled_buffer_11_out), .eq(is_sw));  // open: gt, lt
  not not_2 (not_2_out, is_B);
  not not_3 (not_3_out, is_jal);
  not not_4 (not_4_out, is_jalr);
  assign PCSel = and_4_out ? 1'b0 : 1'bz;  // Controlled_Buffer controlled_buffer_12
  and and_4 (and_4_out, not_2_out, not_3_out, not_4_out);
  not not_5 (not_5_out, BrLt);
  assign PCSel = and_5_out ? not_5_out : 1'bz;  // Controlled_Buffer controlled_buffer_13
  and and_5 (and_5_out, is_bgeu, is_B);
  assign PCSel = and_6_out ? BrLt : 1'bz;  // Controlled_Buffer controlled_buffer_14
  and and_6 (and_6_out, is_bltu, is_B);
  not not_6 (not_6_out, BrLt);
  assign PCSel = and_7_out ? not_6_out : 1'bz;  // Controlled_Buffer controlled_buffer_15
  and and_7 (and_7_out, is_bge, is_B);
  assign PCSel = is_jalr ? 1'b1 : 1'bz;  // Controlled_Buffer controlled_buffer_16

  // Other names for the same wires on the sheet: Funct3[2:0] = Instruction[14:12]; Funct7[6:0] = Instruction[31:25]

  // Notes on the sheet:
  //   INPUTS to your circuit
  //   contents of rom_1 (hex, n*v repeats v):
  //   1001 1401 1601 1081 1481 1581 1101 1201 1281 1681 1301 1381 3041 3041 3041 1041 10c1 1141 1241 12c1
  //   16c1 1341 13c1 842 842 842 4*64 74 74 1067 17c7 2069 2041
  //   ROM FOR CONTROL LOGIC
  //   DON'T CHANGE THE LOCATIONS OF THE INPUTS AND OUTPUTS!
  //   This is only if you choose to do the ROM option
  //   OUTPUT from your circuit
  //   Reminder: If using ROM, use combinational logic for PCSel
endmodule
