// Logisim project imm-gen.circ as structural Verilog: 1 circuit, main circuit imm_gen
module imm_gen (
  input  [31:0] Instruction,
  input  [2:0] ImmSel,
  output [31:0] Immediate
);

  wire is_B, is_I, is_J, is_S, is_U;
  wire [31:0] bit_extender_1_out, bit_extender_2_out, bit_extender_3_out, bit_extender_4_out;

  Demultiplexer #(.select(3)) demultiplexer_1 (
    .out0(is_I), .out1(is_S), .out2(is_B), .out3(is_U), .out4(is_J), .in(1'b1), .sel(ImmSel));  // open: out5, out6, out7
  assign bit_extender_1_out = {{20{Instruction[31]}}, Instruction[31:20]};  // Bit_Extender bit_extender_1
  assign Immediate = is_I ? bit_extender_1_out : 32'bz;  // Controlled_Buffer controlled_buffer_1
  assign bit_extender_2_out = {{20{Instruction[31]}}, {Instruction[31:25], Instruction[11:7]}};  // Bit_Extender bit_extender_2
  assign Immediate = is_S ? bit_extender_2_out : 32'bz;  // Controlled_Buffer controlled_buffer_2
  assign bit_extender_3_out = {{19{Instruction[31]}}, {Instruction[31], Instruction[7], Instruction[30:25], Instruction[11:8], 1'b0}};  // Bit_Extender bit_extender_3
  assign Immediate = is_B ? bit_extender_3_out : 32'bz;  // Controlled_Buffer controlled_buffer_3
  assign Immediate = is_U ? {Instruction[31:12], {12{1'b0}}} : 32'bz;  // Controlled_Buffer controlled_buffer_4
  assign bit_extender_4_out = {{11{Instruction[31]}}, {Instruction[31], Instruction[19:12], Instruction[20], Instruction[30:21], 1'b0}};  // Bit_Extender bit_extender_4
  assign Immediate = is_J ? bit_extender_4_out : 32'bz;  // Controlled_Buffer controlled_buffer_5

  // Notes on the sheet:
  //   INPUTS to your circuit
  //   DON'T CHANGE THE LOCATIONS OF THE INPUTS AND OUTPUTS!
  //   OUTPUT from your circuit
endmodule
