// Logisim project partial-load.circ as structural Verilog: 1 circuit, main circuit partial_load
module partial_load (
  input  [31:0] Instruction,
  input  [31:0] MemAddress,
  input  [31:0] DataFromMem,
  output [31:0] DataToReg
);

  wire demultiplexer_2_out0, demultiplexer_2_out1, demultiplexer_2_out2, demultiplexer_3_out0,
       demultiplexer_3_out1, demultiplexer_3_out2, demultiplexer_3_out3, is_b, is_h, is_w;
  wire [31:0] controlled_buffer_2_out, controlled_buffer_3_out, controlled_buffer_4_out,
       controlled_buffer_5_out, controlled_buffer_6_out, controlled_buffer_7_out, controlled_buffer_8_out;

  Demultiplexer #(.select(3)) demultiplexer_1 (
    .out0(is_b), .out1(is_h), .out2(is_w), .in(1'b1), .sel(Instruction[14:12]));  // open: out3, out4, out5, out6, out7
  assign DataToReg = is_w ? DataFromMem : 32'bz;  // Controlled_Buffer controlled_buffer_1
  Demultiplexer #(.enable("true"), .select(2)) demultiplexer_2 (
    .out0(demultiplexer_2_out0), .out1(demultiplexer_2_out1), .out2(demultiplexer_2_out2), .in(1'b1),
    .sel(MemAddress[1:0]), .en(is_h));  // open: out3
  Demultiplexer #(.enable("true"), .select(2)) demultiplexer_3 (
    .out0(demultiplexer_3_out0), .out1(demultiplexer_3_out1), .out2(demultiplexer_3_out2),
    .out3(demultiplexer_3_out3), .in(1'b1), .sel(MemAddress[1:0]), .en(is_b));
  assign controlled_buffer_2_out = demultiplexer_2_out0 ? DataFromMem : 32'bz;  // Controlled_Buffer controlled_buffer_2
  assign controlled_buffer_3_out = demultiplexer_2_out1 ? DataFromMem : 32'bz;  // Controlled_Buffer controlled_buffer_3
  assign controlled_buffer_4_out = demultiplexer_2_out2 ? DataFromMem : 32'bz;  // Controlled_Buffer controlled_buffer_4
  assign controlled_buffer_5_out = demultiplexer_3_out0 ? DataFromMem : 32'bz;  // Controlled_Buffer controlled_buffer_5
  assign controlled_buffer_6_out = demultiplexer_3_out1 ? DataFromMem : 32'bz;  // Controlled_Buffer controlled_buffer_6
  assign controlled_buffer_7_out = demultiplexer_3_out2 ? DataFromMem : 32'bz;  // Controlled_Buffer controlled_buffer_7
  assign controlled_buffer_8_out = demultiplexer_3_out3 ? DataFromMem : 32'bz;  // Controlled_Buffer controlled_buffer_8
  assign DataToReg = {{16{controlled_buffer_2_out[15]}}, controlled_buffer_2_out[15:0]};  // Bit_Extender bit_extender_1
  assign DataToReg = {{16{controlled_buffer_3_out[23]}}, controlled_buffer_3_out[23:8]};  // Bit_Extender bit_extender_2
  assign DataToReg = {{16{controlled_buffer_4_out[31]}}, controlled_buffer_4_out[31:16]};  // Bit_Extender bit_extender_3
  assign DataToReg = {{24{controlled_buffer_5_out[7]}}, controlled_buffer_5_out[7:0]};  // Bit_Extender bit_extender_4
  assign DataToReg = {{24{controlled_buffer_6_out[15]}}, controlled_buffer_6_out[15:8]};  // Bit_Extender bit_extender_5
  assign DataToReg = {{24{controlled_buffer_7_out[23]}}, controlled_buffer_7_out[23:16]};  // Bit_Extender bit_extender_6
  assign DataToReg = {{24{controlled_buffer_8_out[31]}}, controlled_buffer_8_out[31:24]};  // Bit_Extender bit_extender_7

  // Notes on the sheet:
  //   INPUTS to your circuit
  //   DON'T CHANGE THE LOCATIONS OF THE INPUTS AND OUTPUTS!
  //   OUTPUT from your circuit
endmodule
