// Logisim project partial-store.circ as structural Verilog: 1 circuit, main circuit partial_store
module partial_store (
  input  [31:0] Instruction,
  input  [31:0] MemAddress,
  input  [31:0] DataFromReg,
  input  MemRW,
  output [3:0] MemWriteMask,
  output [31:0] DataToMem
);

  wire and_1_out, and_2_out, and_3_out, and_4_out, demultiplexer_2_out0, demultiplexer_2_out2,
       demultiplexer_3_out0, demultiplexer_3_out1, demultiplexer_3_out2, demultiplexer_3_out3, is_b, is_h,
       is_w, not_1_out;
  wire [31:0] bit_extender_1_out, bit_extender_2_out;

  Demultiplexer #(.select(3)) demultiplexer_1 (
    .out0(is_b), .out1(is_h), .out2(is_w), .in(1'b1), .sel(Instruction[14:12]));  // open: out3, out4, out5, out6, out7
  assign DataToMem = and_1_out ? DataFromReg : 32'bz;  // Controlled_Buffer controlled_buffer_1
  and and_1 (and_1_out, is_w, MemRW);
  assign MemWriteMask = and_2_out ? 4'b1111 : 4'bz;  // Controlled_Buffer controlled_buffer_2
  and and_2 (and_2_out, is_w, MemRW);
  Demultiplexer #(.enable("true"), .select(2)) demultiplexer_2 (
    .out0(demultiplexer_2_out0), .out2(demultiplexer_2_out2), .in(1'b1), .sel(MemAddress[1:0]), .en(and_3_out));  // open: out1, out3
  and and_3 (and_3_out, is_h, MemRW);
  Demultiplexer #(.enable("true"), .select(2)) demultiplexer_3 (
    .out0(demultiplexer_3_out0), .out1(demultiplexer_3_out1), .out2(demultiplexer_3_out2),
    .out3(demultiplexer_3_out3), .in(1'b1), .sel(MemAddress[1:0]), .en(and_4_out));
  and and_4 (and_4_out, is_b, MemRW);
  assign bit_extender_1_out = {{16{DataFromReg[15]}}, DataFromReg[15:0]};  // Bit_Extender bit_extender_1
  assign DataToMem = demultiplexer_2_out0 ? bit_extender_1_out : 32'bz;  // Controlled_Buffer controlled_buffer_3
  assign DataToMem = demultiplexer_2_out2 ? {DataFromReg[15:0], {16{1'b0}}} : 32'bz;  // Controlled_Buffer controlled_buffer_4
  assign bit_extender_2_out = {{24{DataFromReg[7]}}, DataFromReg[7:0]};  // Bit_Extender bit_extender_2
  assign DataToMem = demultiplexer_3_out0 ? bit_extender_2_out : 32'bz;  // Controlled_Buffer controlled_buffer_5
  assign DataToMem = demultiplexer_3_out1 ? {{16{1'b0}}, DataFromReg[7:0], {8{1'b0}}} : 32'bz;  // Controlled_Buffer controlled_buffer_6
  assign DataToMem = demultiplexer_3_out2 ? {{8{1'b0}}, DataFromReg[7:0], {16{1'b0}}} : 32'bz;  // Controlled_Buffer controlled_buffer_7
  assign DataToMem = demultiplexer_3_out3 ? {DataFromReg[7:0], {24{1'b0}}} : 32'bz;  // Controlled_Buffer controlled_buffer_8
  assign MemWriteMask = not_1_out ? 4'b0000 : 4'bz;  // Controlled_Buffer controlled_buffer_9
  not not_1 (not_1_out, MemRW);
  assign MemWriteMask = demultiplexer_2_out0 ? 4'b0011 : 4'bz;  // Controlled_Buffer controlled_buffer_10
  assign MemWriteMask = demultiplexer_2_out2 ? 4'b1100 : 4'bz;  // Controlled_Buffer controlled_buffer_11
  assign MemWriteMask = demultiplexer_3_out0 ? 4'b0001 : 4'bz;  // Controlled_Buffer controlled_buffer_12
  assign MemWriteMask = demultiplexer_3_out1 ? 4'b0010 : 4'bz;  // Controlled_Buffer controlled_buffer_13
  assign MemWriteMask = demultiplexer_3_out2 ? 4'b0100 : 4'bz;  // Controlled_Buffer controlled_buffer_14
  assign MemWriteMask = demultiplexer_3_out3 ? 4'b1000 : 4'bz;  // Controlled_Buffer controlled_buffer_15

  // Notes on the sheet:
  //   INPUTS to your circuit
  //   DON'T CHANGE THE LOCATIONS OF THE INPUTS AND OUTPUTS!
  //   OUTPUT from your circuit
endmodule
