// Logisim project regfile.circ as structural Verilog: 1 circuit, main circuit regfile
module regfile (
  input  [4:0] ReadIndex1,
  input  [4:0] ReadIndex2,
  input  [4:0] WriteIndex,
  input  [31:0] WriteData,
  input  RegWEn,
  input  clk,
  output [31:0] ra,
  output [31:0] sp,
  output [31:0] t0,
  output [31:0] t1,
  output [31:0] t2,
  output [31:0] s0,
  output [31:0] s1,
  output [31:0] a0,
  output [31:0] ReadData1,
  output [31:0] ReadData2
);

  wire demultiplexer_1_out1, demultiplexer_1_out2, demultiplexer_1_out3, demultiplexer_1_out4,
       demultiplexer_1_out5, demultiplexer_1_out6, demultiplexer_1_out7, demultiplexer_1_out8,
       demultiplexer_1_out9, demultiplexer_1_out10, demultiplexer_1_out11, demultiplexer_1_out12,
       demultiplexer_1_out13, demultiplexer_1_out14, demultiplexer_1_out15, demultiplexer_1_out16,
       demultiplexer_1_out17, demultiplexer_1_out18, demultiplexer_1_out19, demultiplexer_1_out20,
       demultiplexer_1_out21, demultiplexer_1_out22, demultiplexer_1_out23, demultiplexer_1_out24,
       demultiplexer_1_out25, demultiplexer_1_out26, demultiplexer_1_out27, demultiplexer_1_out28,
       demultiplexer_1_out29, demultiplexer_1_out30, demultiplexer_1_out31;
  wire [31:0] a1, a2, a3, a4, a5, a6, a7, demultiplexer_2_out0, demultiplexer_2_out1, demultiplexer_2_out2,
       demultiplexer_2_out3, demultiplexer_2_out4, demultiplexer_2_out5, demultiplexer_2_out6,
       demultiplexer_2_out7, demultiplexer_2_out8, demultiplexer_2_out9, demultiplexer_2_out10,
       demultiplexer_2_out11, demultiplexer_2_out12, demultiplexer_2_out13, demultiplexer_2_out14,
       demultiplexer_2_out15, demultiplexer_2_out16, demultiplexer_2_out17, demultiplexer_2_out18,
       demultiplexer_2_out19, demultiplexer_2_out20, demultiplexer_2_out21, demultiplexer_2_out22,
       demultiplexer_2_out23, demultiplexer_2_out24, demultiplexer_2_out25, demultiplexer_2_out26,
       demultiplexer_2_out27, demultiplexer_2_out28, demultiplexer_2_out29, demultiplexer_2_out30,
       demultiplexer_2_out31, gp, register_28_q, s2, s3, s4, s5, s6, s7, s8, s9, s10, s11, t3, t4, t5, t6, tp;

  Multiplexer #(.select(5), .width(32)) multiplexer_1 (
    .in0({32{1'b0}}), .in1(ra), .in2(sp), .in3(gp), .in4(tp), .in5(t0), .in6(t1), .in7(t2), .in8(s0),
    .in9(s1), .in10(a0), .in11(a1), .in12(a2), .in13(a3), .in14(a4), .in15(a5), .in16(a6), .in17(a7),
    .in18(s2), .in19(s3), .in20(s4), .in21(s5), .in22(s6), .in23(s7), .in24(s8), .in25(s9), .in26(s10),
    .in27(s11), .in28(t3), .in29(t4), .in30(t5), .in31(t6), .out(ReadData1), .sel(ReadIndex1));
  Multiplexer #(.select(5), .width(32)) multiplexer_2 (
    .in0({32{1'b0}}), .in1(ra), .in2(sp), .in3(gp), .in4(tp), .in5(t0), .in6(t1), .in7(t2), .in8(s0),
    .in9(s1), .in10(a0), .in11(a1), .in12(a2), .in13(a3), .in14(a4), .in15(a5), .in16(a6), .in17(a7),
    .in18(s2), .in19(s3), .in20(s4), .in21(s5), .in22(s6), .in23(s7), .in24(s8), .in25(s9), .in26(s10),
    .in27(s11), .in28(t3), .in29(t4), .in30(t5), .in31(t6), .out(ReadData2), .sel(ReadIndex2));
  Demultiplexer #(.select(5)) demultiplexer_1 (
    .out1(demultiplexer_1_out1), .out2(demultiplexer_1_out2), .out3(demultiplexer_1_out3),
    .out4(demultiplexer_1_out4), .out5(demultiplexer_1_out5), .out6(demultiplexer_1_out6),
    .out7(demultiplexer_1_out7), .out8(demultiplexer_1_out8), .out9(demultiplexer_1_out9),
    .out10(demultiplexer_1_out10), .out11(demultiplexer_1_out11), .out12(demultiplexer_1_out12),
    .out13(demultiplexer_1_out13), .out14(demultiplexer_1_out14), .out15(demultiplexer_1_out15),
    .out16(demultiplexer_1_out16), .out17(demultiplexer_1_out17), .out18(demultiplexer_1_out18),
    .out19(demultiplexer_1_out19), .out20(demultiplexer_1_out20), .out21(demultiplexer_1_out21),
    .out22(demultiplexer_1_out22), .out23(demultiplexer_1_out23), .out24(demultiplexer_1_out24),
    .out25(demultiplexer_1_out25), .out26(demultiplexer_1_out26), .out27(demultiplexer_1_out27),
    .out28(demultiplexer_1_out28), .out29(demultiplexer_1_out29), .out30(demultiplexer_1_out30),
    .out31(demultiplexer_1_out31), .in(RegWEn), .sel(WriteIndex));  // open: out0
  Demultiplexer #(.select(5), .width(32)) demultiplexer_2 (
    .out0(demultiplexer_2_out0), .out1(demultiplexer_2_out1), .out2(demultiplexer_2_out2),
    .out3(demultiplexer_2_out3), .out4(demultiplexer_2_out4), .out5(demultiplexer_2_out5),
    .out6(demultiplexer_2_out6), .out7(demultiplexer_2_out7), .out8(demultiplexer_2_out8),
    .out9(demultiplexer_2_out9), .out10(demultiplexer_2_out10), .out11(demultiplexer_2_out11),
    .out12(demultiplexer_2_out12), .out13(demultiplexer_2_out13), .out14(demultiplexer_2_out14),
    .out15(demultiplexer_2_out15), .out16(demultiplexer_2_out16), .out17(demultiplexer_2_out17),
    .out18(demultiplexer_2_out18), .out19(demultiplexer_2_out19), .out20(demultiplexer_2_out20),
    .out21(demultiplexer_2_out21), .out22(demultiplexer_2_out22), .out23(demultiplexer_2_out23),
    .out24(demultiplexer_2_out24), .out25(demultiplexer_2_out25), .out26(demultiplexer_2_out26),
    .out27(demultiplexer_2_out27), .out28(demultiplexer_2_out28), .out29(demultiplexer_2_out29),
    .out30(demultiplexer_2_out30), .out31(demultiplexer_2_out31), .in(WriteData), .sel(WriteIndex));
  Register #(.width(32)) register_1 (
    .D(demultiplexer_2_out1), .en(demultiplexer_1_out1), .clk(clk), .Q(ra));  // open: clr
  Register #(.width(32)) register_2 (
    .D(demultiplexer_2_out2), .en(demultiplexer_1_out2), .clk(clk), .Q(sp));  // open: clr
  Register #(.width(32)) register_3 (
    .D(demultiplexer_2_out3), .en(demultiplexer_1_out3), .clk(clk), .Q(gp));  // open: clr
  Register #(.width(32)) register_4 (
    .D(demultiplexer_2_out4), .en(demultiplexer_1_out4), .clk(clk), .Q(tp));  // open: clr
  Register #(.width(32)) register_5 (
    .D(demultiplexer_2_out5), .en(demultiplexer_1_out5), .clk(clk), .Q(t0));  // open: clr
  Register #(.width(32)) register_6 (
    .D(demultiplexer_2_out6), .en(demultiplexer_1_out6), .clk(clk), .Q(t1));  // open: clr
  Register #(.width(32)) register_7 (
    .D(demultiplexer_2_out7), .en(demultiplexer_1_out7), .clk(clk), .Q(t2));  // open: clr
  Register #(.width(32)) register_8 (
    .D(demultiplexer_2_out8), .en(demultiplexer_1_out8), .clk(clk), .Q(s0));  // open: clr
  Register #(.width(32)) register_9 (
    .D(demultiplexer_2_out9), .en(demultiplexer_1_out9), .clk(clk), .Q(s1));  // open: clr
  Register #(.width(32)) register_10 (
    .D(demultiplexer_2_out10), .en(demultiplexer_1_out10), .clk(clk), .Q(a0));  // open: clr
  Register #(.width(32)) register_11 (
    .D(demultiplexer_2_out11), .en(demultiplexer_1_out11), .clk(clk), .Q(a1));  // open: clr
  Register #(.width(32)) register_12 (
    .D(demultiplexer_2_out12), .en(demultiplexer_1_out12), .clk(clk), .Q(a2));  // open: clr
  Register #(.width(32)) register_13 (
    .D(demultiplexer_2_out13), .en(demultiplexer_1_out13), .clk(clk), .Q(a3));  // open: clr
  Register #(.width(32)) register_14 (
    .D(demultiplexer_2_out14), .en(demultiplexer_1_out14), .clk(clk), .Q(a4));  // open: clr
  Register #(.width(32)) register_15 (
    .D(demultiplexer_2_out15), .en(demultiplexer_1_out15), .clk(clk), .Q(a5));  // open: clr
  Register #(.width(32)) register_16 (
    .D(demultiplexer_2_out16), .en(demultiplexer_1_out16), .clk(clk), .Q(a6));  // open: clr
  Register #(.width(32)) register_17 (
    .D(demultiplexer_2_out17), .en(demultiplexer_1_out17), .clk(clk), .Q(a7));  // open: clr
  Register #(.width(32)) register_18 (
    .D(demultiplexer_2_out18), .en(demultiplexer_1_out18), .clk(clk), .Q(s2));  // open: clr
  Register #(.width(32)) register_19 (
    .D(demultiplexer_2_out19), .en(demultiplexer_1_out19), .clk(clk), .Q(s3));  // open: clr
  Register #(.width(32)) register_20 (
    .D(demultiplexer_2_out20), .en(demultiplexer_1_out20), .clk(clk), .Q(s4));  // open: clr
  Register #(.width(32)) register_21 (
    .D(demultiplexer_2_out21), .en(demultiplexer_1_out21), .clk(clk), .Q(s5));  // open: clr
  Register #(.width(32)) register_22 (
    .D(demultiplexer_2_out22), .en(demultiplexer_1_out22), .clk(clk), .Q(s6));  // open: clr
  Register #(.width(32)) register_23 (.D(demultiplexer_2_out23), .en(demultiplexer_1_out23), .Q(s7));  // open: clk, clr
  Register #(.width(32)) register_24 (
    .D(demultiplexer_2_out24), .en(demultiplexer_1_out24), .clk(clk), .Q(s8));  // open: clr
  Register #(.width(32)) register_25 (
    .D(demultiplexer_2_out25), .en(demultiplexer_1_out25), .clk(clk), .Q(s9));  // open: clr
  Register #(.width(32)) register_26 (
    .D(demultiplexer_2_out26), .en(demultiplexer_1_out26), .clk(clk), .Q(s10));  // open: clr
  Register #(.width(32)) register_27 (
    .D(demultiplexer_2_out27), .en(demultiplexer_1_out27), .clk(clk), .Q(s11));  // open: clr
  Register #(.width(32)) register_28 (
    .D(demultiplexer_2_out28), .en(demultiplexer_1_out28), .clk(clk), .Q(register_28_q));  // open: clr
  Register #(.width(32)) register_29 (
    .D(demultiplexer_2_out29), .en(demultiplexer_1_out29), .clk(clk), .Q(t4));  // open: clr
  Register #(.width(32)) register_30 (
    .D(demultiplexer_2_out30), .en(demultiplexer_1_out30), .clk(clk), .Q(t5));  // open: clr
  Register #(.width(32)) register_31 (
    .D(demultiplexer_2_out31), .en(demultiplexer_1_out31), .clk(clk), .Q(t6));  // open: clr

  // Notes on the sheet:
  //   INPUTS to your circuit
  //   DON'T CHANGE THE LOCATIONS OF THE INPUTS AND OUTPUTS!
  //   These are DEBUG/TEST outputs from your circuit.
  //   OUTPUTS from your circuit
endmodule
